// Logisim project Stack Simulation.circ as structural Verilog: 3 circuits, main circuit Main
module Main (
  input  Post_Pre,
  input  Clr,
  input  [7:0] Input,
  input  Inp_Opr,
  input  Select,
  input  [1:0] Operations,
  output [7:0] Carry_O_P,
  output [7:0] O_P,
  output [7:0] out_9
);

  wire adder_1_cout, and_5_out, and_6_out, Clock_for_O_P_Reg_out, Clock_out, decoder_1_out0, decoder_1_out1,
       decoder_1_out2, decoder_1_out3, not_1_out, not_2_out, or_2_out, subtractor_1_bout;
  wire [7:0] adder_1_out, and_1_out, and_2_out, and_3_out, and_4_out, and_7_out, and_8_out, divider_1_out,
       divider_1_rem, multiplexer_2_out, multiplexer_3_out, multiplexer_4_out, multiplexer_5_out,
       multiplexer_6_out, multiplexer_7_out, multiplexer_8_out, multiplier_1_cout, multiplier_1_out,
       or_1_out, or_4_out, Reg_A_q, Reg_B_q, Stack_pop_o_p, subtractor_1_out;

  Multiplexer #(.width(8)) multiplexer_1 (.in0(Input), .in1(O_P), .out(out_9), .sel(Select));  // open: en
  Clock Clock (.out(Clock_out));
  Stack Stack (.Input(out_9), .Push_Pop(Inp_Opr), .Pop_O_P(Stack_pop_o_p), .Clock(Clock_out));
  Multiplexer #(.width(8)) multiplexer_2 (
    .in0({8{1'b0}}), .in1({8{1'b1}}), .out(multiplexer_2_out), .sel(decoder_1_out2));  // open: en
  Multiplexer #(.width(8)) multiplexer_3 (
    .in0({8{1'b0}}), .in1({8{1'b1}}), .out(multiplexer_3_out), .sel(decoder_1_out3));  // open: en
  Multiplexer #(.width(8)) multiplexer_4 (
    .in0(Reg_B_q), .in1(Reg_A_q), .out(multiplexer_4_out), .sel(Post_Pre));  // open: en
  not not_1 (not_1_out, Post_Pre);
  Multiplexer #(.width(8)) multiplexer_5 (
    .in0(Reg_B_q), .in1(Reg_A_q), .out(multiplexer_5_out), .sel(not_1_out));  // open: en
  Decoder #(.select(2)) decoder_1 (
    .out0(decoder_1_out0), .out1(decoder_1_out1), .out2(decoder_1_out2), .out3(decoder_1_out3),
    .sel(Operations));  // open: en
  Register Reg_A (.D(Stack_pop_o_p), .Q(Reg_A_q), .clk(not_2_out), .clr(Clr));  // open: en
  Adder adder_1 (.a(multiplexer_4_out), .b(multiplexer_5_out), .out(adder_1_out), .cout(adder_1_cout));  // open: cin
  Subtractor subtractor_1 (
    .a(multiplexer_4_out), .b(multiplexer_5_out), .out(subtractor_1_out), .bout(subtractor_1_bout));  // open: bin
  Multiplier multiplier_1 (
    .a(multiplexer_4_out), .b(multiplexer_5_out), .out(multiplier_1_out), .cout(multiplier_1_cout));  // open: cin
  Divider divider_1 (
    .a(multiplexer_4_out), .b(multiplexer_5_out), .out(divider_1_out), .upper(multiplexer_4_out),
    .rem(divider_1_rem));
  Register Reg_B (.D(Reg_A_q), .Q(Reg_B_q), .clk(not_2_out), .clr(Clr));  // open: en
  not not_2 (not_2_out, Clock_out);
  assign and_1_out = divider_1_out & multiplexer_3_out;  // AND_Gate and_1, 8 bits wide
  Multiplexer #(.width(8)) multiplexer_6 (
    .in0({8{1'b0}}), .in1({8{1'b1}}), .out(multiplexer_6_out), .sel(decoder_1_out0));  // open: en
  Register register_1 (.D(or_1_out), .Q(O_P), .clk(Clock_for_O_P_Reg_out));  // open: en, clr
  assign or_1_out = and_2_out | and_3_out | and_4_out | and_1_out;  // OR_Gate or_1, 8 bits wide
  assign and_2_out = adder_1_out & multiplexer_6_out;  // AND_Gate and_2, 8 bits wide
  assign and_3_out = subtractor_1_out & multiplexer_7_out;  // AND_Gate and_3, 8 bits wide
  assign and_4_out = multiplier_1_out & multiplexer_2_out;  // AND_Gate and_4, 8 bits wide
  Multiplexer #(.width(8)) multiplexer_7 (
    .in0({8{1'b0}}), .in1({8{1'b1}}), .out(multiplexer_7_out), .sel(decoder_1_out1));  // open: en
  Clock Clock_for_O_P_Reg (.out(Clock_for_O_P_Reg_out));
  and and_5 (and_5_out, adder_1_cout, decoder_1_out0);
  and and_6 (and_6_out, subtractor_1_bout, decoder_1_out1);
  or or_2 (or_2_out, and_5_out, and_6_out);
  assign and_7_out = multiplexer_2_out & multiplier_1_cout;  // AND_Gate and_7, 8 bits wide
  assign and_8_out = divider_1_rem & multiplexer_3_out;  // AND_Gate and_8, 8 bits wide
  assign Carry_O_P = multiplexer_8_out | or_4_out;  // OR_Gate or_3, 8 bits wide
  Multiplexer #(.width(8)) multiplexer_8 (
    .in0({8{1'b0}}), .in1(8'h1), .out(multiplexer_8_out), .sel(or_2_out));  // open: en
  assign or_4_out = and_7_out | and_8_out;  // OR_Gate or_4, 8 bits wide

  // Notes on the sheet:
  //   1 - Push
  //   0 - Pop
  //   What is to be loaded
  //   1 - Postfix
  //   0 - Prefix
  //   Operations
  //   0 - Addition
  //   1 - Subtract
  //   2 - Multiplication
  //   3 - Division
endmodule

module Stack (
  input  [7:0] Input,
  input  Push_Pop,
  input  Clock,
  output [7:0] Pop_O_P
);

  wire Controller_read_decr, Controller_sc_clr, Controller_sc_inc, Controller_top_inc, Controller_write,
       Counter_q, decoder_1_out0, decoder_1_out1;
  wire [7:0] ram_1_data, Top_q;

  Decoder #(.enable("false")) decoder_1 (.out0(decoder_1_out0), .out1(decoder_1_out1), .sel(Counter_q));
  Counter #(.width(1), .max('h1)) Counter (
    .load(Controller_sc_clr), .D(1'b0), .count(Controller_sc_inc), .Q(Counter_q), .clk(Clock));  // open: carry, clr
  Controller Controller (
    .Push_Pop(Push_Pop), .O_P_0(decoder_1_out0), .O_P_1(decoder_1_out1), .Top_Inc(Controller_top_inc),
    .Write(Controller_write), .Read_Decr(Controller_read_decr), .SC_Clr(Controller_sc_clr), .Top_Val(Top_q),
    .SC_Inc(Controller_sc_inc));
  Counter #(.ongoal("stay")) Top (
    .load(Controller_read_decr), .count(Controller_top_inc), .Q(Top_q), .clk(Clock));  // open: D, carry, clr
  RAM #(.bus("separate")) ram_1 (
    .addr(Top_q), .din(Input), .data(ram_1_data), .str(Controller_write), .clk(Clock),
    .ld(Controller_read_decr));  // open: sel, clr
  Register Pop (.D(ram_1_data), .en(Controller_read_decr), .Q(Pop_O_P), .clk(Clock));  // open: clr

  // Notes on the sheet:
  //   1 - Push
  //   0 - Pop
endmodule

module Controller (
  input  Push_Pop,
  input  O_P_0,
  input  O_P_1,
  input  [7:0] Top_Val,
  output Top_Inc,
  output Write,
  output SC_Clr,
  output Read_Decr,
  output SC_Inc
);

  wire and_1_out, and_3_out, and_4_out, not_1_out, not_2_out, not_3_out, not_4_out, not_5_out, not_6_out;

  and and_1 (and_1_out, Push_Pop, O_P_0);
  and and_2 (Write, Push_Pop, O_P_1);
  not not_1 (not_1_out, Push_Pop);
  not not_2 (not_2_out, Top_Val[4]);
  not not_3 (not_3_out, Top_Val[5]);
  not not_4 (not_4_out, Top_Val[6]);
  not not_5 (not_5_out, Top_Val[7]);
  and and_3 (and_3_out, O_P_0, not_1_out);
  and and_4 (and_4_out, and_1_out, Top_Val[0], Top_Val[1], Top_Val[2], Top_Val[3], not_2_out, not_3_out, not_4_out, not_5_out);
  or or_1 (Read_Decr, and_3_out, and_4_out);
  or or_2 (SC_Clr, Write, Read_Decr);
  not not_6 (not_6_out, Read_Decr);
  or or_3 (Top_Inc, and_1_out, Read_Decr);
  and and_5 (SC_Inc, and_1_out, not_6_out);
endmodule
